// Logisim project Guia_0501.circ as structural Verilog: 1 circuit, main circuit main
module main (
  input  a,
  input  b,
  input  a_2,
  input  b_2,
  input  a_3,
  input  b_3,
  input  a_4,
  input  b_4,
  output out_9,
  output out_10,
  output out_11,
  output out_12
);

  wire nor_1_out, nor_2_out, nor_3_out, nor_4_out, nor_5_out, nor_6_out, nor_7_out, nor_8_out, nor_9_out,
       nor_10_out, nor_11_out, nor_12_out;

  nor nor_1 (nor_1_out, nor_2_out, nor_2_out);
  nor nor_2 (nor_2_out, a, a);
  nor nor_3 (nor_3_out, b, b);
  nor nor_4 (nor_4_out, a_2, a_2);
  nor nor_5 (nor_5_out, nor_4_out, nor_4_out);
  nor nor_6 (nor_6_out, b_2, b_2);
  nor nor_7 (nor_7_out, a_3, a_3);
  nor nor_8 (nor_8_out, nor_7_out, nor_7_out);
  nor nor_9 (nor_9_out, b_3, b_3);
  nor nor_10 (nor_10_out, a_4, a_4);
  nor nor_11 (nor_11_out, nor_10_out, nor_10_out);
  nor nor_12 (nor_12_out, b_4, b_4);
  nor nor_13 (out_9, nor_1_out, nor_3_out);
  nor nor_14 (out_10, nor_5_out, nor_6_out);
  nor nor_15 (out_11, nor_8_out, nor_9_out);
  nor nor_16 (out_12, nor_11_out, nor_12_out);
endmodule
