// Logisim project Guia_0503.circ as structural Verilog: 1 circuit, main circuit main
module main (
  input  a,
  input  b,
  input  a_2,
  input  b_2,
  input  a_3,
  input  b_3,
  input  a_4,
  input  b_4,
  output out_9,
  output out_10,
  output out_11,
  output out_12
);

  wire nor_1_out, nor_3_out, nor_5_out, nor_7_out;

  nor nor_1 (nor_1_out, a, a);
  nor nor_2 (out_9, nor_1_out, b);
  nor nor_3 (nor_3_out, a_2, a_2);
  nor nor_4 (out_10, nor_3_out, b_2);
  nor nor_5 (nor_5_out, a_3, a_3);
  nor nor_6 (out_11, nor_5_out, b_3);
  nor nor_7 (nor_7_out, a_4, a_4);
  nor nor_8 (out_12, nor_7_out, b_4);
endmodule
