// Logisim project Guia_0504.circ as structural Verilog: 1 circuit, main circuit main
module main (
  input  a,
  input  b,
  input  a_2,
  input  b_2,
  input  a_3,
  input  b_3,
  input  a_4,
  input  b_4,
  output out_9,
  output out_10,
  output out_11,
  output out_12
);

  wire nand_1_out, nand_2_out, nand_3_out, nand_4_out;

  nand nand_1 (nand_1_out, a, a);
  nand nand_2 (nand_2_out, a_2, a_2);
  nand nand_3 (nand_3_out, a_3, a_3);
  nand nand_4 (nand_4_out, a_4, a_4);
  nand nand_5 (out_9, nand_1_out, b);
  nand nand_6 (out_10, nand_2_out, b_2);
  nand nand_7 (out_11, nand_3_out, b_3);
  nand nand_8 (out_12, nand_4_out, b_4);
endmodule
