// Logisim project Guia_0505.circ as structural Verilog: 1 circuit, main circuit main
module main (
  input  in_1,
  input  in_2,
  input  in_3,
  input  in_4,
  input  in_5,
  input  in_6,
  input  in_7,
  input  in_8,
  output out_9,
  output out_10,
  output out_11,
  output out_12
);

  wire nor_1_out, nor_2_out, nor_3_out, nor_4_out, nor_5_out, nor_6_out, nor_7_out, nor_8_out, nor_9_out,
       nor_10_out, nor_11_out, nor_12_out;

  nor nor_1 (nor_1_out, in_1, in_2);
  nor nor_2 (nor_2_out, in_3, in_4);
  nor nor_3 (nor_3_out, in_5, in_6);
  nor nor_4 (nor_4_out, in_7, in_8);
  nor nor_5 (nor_5_out, in_1, nor_1_out);
  nor nor_6 (nor_6_out, nor_1_out, in_2);
  nor nor_7 (nor_7_out, in_3, nor_2_out);
  nor nor_8 (nor_8_out, nor_2_out, in_4);
  nor nor_9 (nor_9_out, in_5, nor_3_out);
  nor nor_10 (nor_10_out, nor_3_out, in_6);
  nor nor_11 (nor_11_out, in_7, nor_4_out);
  nor nor_12 (nor_12_out, nor_4_out, in_8);
  nor nor_13 (out_9, nor_5_out, nor_6_out);
  nor nor_14 (out_10, nor_7_out, nor_8_out);
  nor nor_15 (out_11, nor_9_out, nor_10_out);
  nor nor_16 (out_12, nor_11_out, nor_12_out);
endmodule
