// Logisim project Guia_0506.circ as structural Verilog: 1 circuit, main circuit main
module main (
  input  in_1,
  input  in_2,
  input  in_3,
  input  in_4,
  input  in_5,
  input  in_6,
  input  in_7,
  input  in_8,
  output out_9,
  output out_10,
  output out_11,
  output out_12
);

  wire nand_1_out, nand_2_out, nand_3_out, nand_4_out, nand_5_out, nand_6_out, nand_7_out, nand_8_out,
       nand_9_out, nand_10_out, nand_11_out, nand_12_out;

  nand nand_1 (nand_1_out, in_1, in_2);
  nand nand_2 (nand_2_out, in_3, in_4);
  nand nand_3 (nand_3_out, in_5, in_6);
  nand nand_4 (nand_4_out, in_7, in_8);
  nand nand_5 (nand_5_out, in_1, nand_1_out);
  nand nand_6 (nand_6_out, nand_1_out, in_2);
  nand nand_7 (nand_7_out, in_3, nand_2_out);
  nand nand_8 (nand_8_out, nand_2_out, in_4);
  nand nand_9 (nand_9_out, in_5, nand_3_out);
  nand nand_10 (nand_10_out, nand_3_out, in_6);
  nand nand_11 (nand_11_out, in_7, nand_4_out);
  nand nand_12 (nand_12_out, nand_4_out, in_8);
  nand nand_13 (out_9, nand_5_out, nand_6_out);
  nand nand_14 (out_10, nand_7_out, nand_8_out);
  nand nand_15 (out_11, nand_9_out, nand_10_out);
  nand nand_16 (out_12, nand_11_out, nand_12_out);
endmodule
