// Logisim project Guia17_01.circ as structural Verilog: 1 circuit, main circuit main
module main (
  input  c,
  input  clk
);

  wire and_1_out, and_2_out, and_3_out, and_4_out, and_5_out, d_ff_1_q, d_ff_2_q, or_1_out, or_2_out;

  and and_1 (and_1_out, ~d_ff_1_q, d_ff_2_q, c);  // AND_Gate
  and and_2 (and_2_out, d_ff_1_q, ~d_ff_2_q, ~c);  // AND_Gate
  and and_3 (and_3_out, d_ff_2_q, d_ff_1_q);
  and and_4 (and_4_out, c, ~d_ff_1_q);  // AND_Gate
  and and_5 (and_5_out, ~d_ff_1_q, c);  // AND_Gate
  or or_1 (or_1_out, and_1_out, and_2_out, and_3_out);
  or or_2 (or_2_out, and_4_out, and_5_out);
  D_Flip_Flop #(.Pre_Clr_Positions("LEGACY"), .enable("true")) d_ff_1 (
    .clk(clk), .D(or_1_out), .Q(d_ff_1_q));  // open: Qn, preset, en, reset
  D_Flip_Flop d_ff_2 (.clk(clk), .D(or_2_out), .Q(d_ff_2_q));  // open: Qn, preset, reset

  // Notes on the sheet:
  //   a'b + a'c
  //   a'bc + ab'c' + ab
  //   s1 = a
  //   s2 = b
endmodule
