// Logisim project Guia17_02.circ as structural Verilog: 1 circuit, main circuit main
module main (
  input  c,
  input  clk
);

  wire and_1_out, and_2_out, and_3_out, and_4_out, j_k_ff_1_q, j_k_ff_2_q;

  and and_1 (and_1_out, ~j_k_ff_1_q, j_k_ff_2_q, c);  // AND_Gate
  and and_2 (and_2_out, j_k_ff_1_q, ~j_k_ff_2_q, c);  // AND_Gate
  and and_3 (and_3_out, ~j_k_ff_1_q, ~j_k_ff_2_q, c);  // AND_Gate
  and and_4 (and_4_out, j_k_ff_1_q, j_k_ff_2_q, c);
  J_K_Flip_Flop j_k_ff_1 (.J(and_1_out), .clk(clk), .K(and_2_out), .Q(j_k_ff_1_q));  // open: Qn, preset, reset
  J_K_Flip_Flop j_k_ff_2 (.J(and_3_out), .clk(clk), .K(and_4_out), .Q(j_k_ff_2_q));  // open: Qn, preset, reset

  // Notes on the sheet:
  //   s1 = a
  //   s2 = b
endmodule
