// Logisim project Guia17_04.circ as structural Verilog: 1 circuit, main circuit main
module main (
  input  load,
  input  clk,
  output out_3,
  output out_4,
  output out_5
);

  T_Flip_Flop #(.Pre_Clr_Positions("LEGACY"), .enable("true"), .NewFFLayout("false")) t_ff_1 (
    .clk(clk), .T(load), .Q(out_5));  // open: Qn, preset, reset, en
  T_Flip_Flop #(.Pre_Clr_Positions("LEGACY"), .enable("true"), .NewFFLayout("false")) t_ff_2 (
    .clk(out_5), .T(load), .Q(out_4));  // open: Qn, preset, reset, en
  T_Flip_Flop #(.Pre_Clr_Positions("LEGACY"), .enable("true"), .NewFFLayout("false")) t_ff_3 (
    .clk(out_4), .T(load), .Q(out_3));  // open: Qn, preset, reset, en
endmodule
